# Fritzing sketch Buzzer (saved by Fritzing 0.9.0b)
breadboards: 1

parts:
  Part1 = Arduino Uno (Rev3)
  J1 = Piezo Speaker
  U1 = POT [package=trim_pot]
  R1 = Resistor [tolerance=±5% resistance=12k package=THT]

nets:
  N1: Part1.A0, U1.E
  N2: Part1.D13/SCK, R1.Pin_0
  N3: Part1.GND, J1.pin1, U1.A
  N4: Part1.5V, U1.S
  N5: J1.pin2, R1.Pin_1
