# Fritzing sketch blink2 (saved by Fritzing 0.9.0b)
breadboards: 1

parts:
  Part1 = Arduino Uno (Rev3)
  LED1 = smd LED [color="Red (633nm)" package="0805 [SMD]"]
  LED2 = smd LED [color="Red (633nm)" package="0805 [SMD]"]
  R1 = Resistor [tolerance=±5% resistance=150 package=THT]
  R2 = Resistor [tolerance=±5% resistance=150 package=THT]

nets:
  N1: Part1.D12/MISO, LED2.cathode
  N2: Part1.D13/SCK, LED1.anode
  N3: Part1.GND, R2.Pin_0
  N4: Part1.5V, R1.Pin_1
  N5: LED1.cathode, R2.Pin_1
  N6: LED2.anode, R1.Pin_0
