# Fritzing sketch pin_source (saved by Fritzing 0.9.0b)
breadboards: 1

parts:
  LED1 = LED - 5mm [color="Red (633nm)" package="5 mm [THT]"]
  Part1 = Arduino Uno (Rev3)
  R1 = Resistor [tolerance=±5% resistance=150 package=THT]

nets:
  N1: LED1.cathode, R1.Pin_1
  N2: LED1.anode, Part1.D13/SCK
  N3: Part1.GND, R1.Pin_0
